# Fritzing sketch gioco delle forme wifi tablet circuito (saved by Fritzing 0.9.3b)

parts:
  WeMos_D1_Mini1 = WeMos D1 Mini
  U1 = BATTERY-2 [package=battery-aa]
  U2 = BATTERY-2 [package=battery-aa]
  U3 = BATTERY-2 [package=battery-aa]
  U4 = BATTERY-2 [package=battery-aa]
  Componente1 = Arduino Nano (Rev3.0)
  LED1 = LED - 5mm [color="Blue (525nm)" package="5 mm [THT]"]
  LED2 = LED - 5mm [color="Blue (525nm)" package="5 mm [THT]"]
  LED3 = LED - 5mm [color="Blue (525nm)" package="5 mm [THT]"]
  LED4 = LED - 5mm [color="Blue (525nm)" package="5 mm [THT]"]
  LED5 = LED - 5mm [color="Blue (525nm)" package="5 mm [THT]"]
  R1 = Resistor [tolerance=±5% resistance=2.2k package=THT]
  R2 = Resistor [tolerance=±5% resistance=2.2k package=THT]
  R3 = Resistor [tolerance=±5% resistance=2.2k package=THT]
  R4 = Resistor [tolerance=±5% resistance=2.2k package=THT]
  R5 = Resistor [tolerance=±5% resistance=2.2k package=THT]
  U11 = SWITCH_SPDT [package=kps-1290]
  LLC1 = Logic Level Converter [package="Breakout board"]
  Part1 = KY-003 Hall Magnetic Sensor Module [package="Breakout board"]
  Part2 = KY-003 Hall Magnetic Sensor Module [package="Breakout board"]
  Part3 = KY-003 Hall Magnetic Sensor Module [package="Breakout board"]
  Part4 = KY-003 Hall Magnetic Sensor Module [package="Breakout board"]
  Part5 = KY-003 Hall Magnetic Sensor Module [package="Breakout board"]

nets:
  N1: WeMos_D1_Mini1.3V3, LLC1.LV
  VIN: WeMos_D1_Mini1.5V, Componente1.5V, U11.S, LLC1.HV, Part1.Vin, Part2.Vin, Part3.Vin, Part4.Vin, Part5.Vin
  N2: WeMos_D1_Mini1.D1, LLC1.LV1
  N3: WeMos_D1_Mini1.D2, LLC1.LV2
  N4: WeMos_D1_Mini1.G, U4.-2, Componente1.GND, LED1.cathode, LED2.cathode, LED3.cathode, LLC1.L-GND, LLC1.H-GND, Part1.-, Part2.-, Part3.-, Part4.-, Part5.-
  N5: U1.-1, U2.+1
  N6: U1.+1, U11.P
  N7: U2.-2, U3.+2
  N8: U3.-1, U4.+1
  N9: U4.-1, LED4.cathode, LED5.cathode
  N10: Componente1.D4, R1.Pin_1
  N11: Componente1.D5, R2.Pin_1
  N12: Componente1.D6, R3.Pin_1
  N13: Componente1.D7, R4.Pin_1
  N14: Componente1.D8, R5.Pin_1
  N15: Componente1.D10, LLC1.HV2
  N16: Componente1.D11/MOSI, LLC1.HV1
  N17: Componente1.A4, Part5.S
  N18: Componente1.A3, Part4.S
  N19: Componente1.A2, Part3.S
  N20: Componente1.A1, Part2.S
  N21: Componente1.A0, Part1.S
  N22: LED1.anode, R1.Pin_0
  N23: LED2.anode, R2.Pin_0
  N24: LED3.anode, R3.Pin_0
  N25: LED4.anode, R4.Pin_0
  N26: LED5.anode, R5.Pin_0

custom parts:
  Logic Level Converter: 5V to/from 3.3V logic level converter
  KY-003 Hall Magnetic Sensor Module: KEYES KY-003 Arduino Hall Magnetic Sensor Module is a switch that will turn on/off in the presence of a magnetic field.
